# Fritzing sketch схема (saved by Fritzing 0.9.3b)
breadboards: 1

parts:
  U1 = NodeMCU V3.0
  DHT1 = DHT11 Humitidy and Temperature Sensor
  LED1 = LED - 3mm [color="Red (633nm)" package="3 mm [THT]"]
  R1 = Resistor [tolerance=±5% resistance=220 package="0402 [SMD]"]
  Q1 = PNP-Transistor [package="TO92 [THT]"]
  M1 = DC Motor
  U3 = LIPO-110mAh [package=lipo-110]

nets:
  N1: U1.D1, DHT1.DATA
  N2: U1.D2, LED1.anode
  N3: U1.D3, Q1.B
  3V3: U1.3V3, DHT1.VDD
  GND: U1.GND, DHT1.GND, R1.Pin_0, Q1.C, U3.-
  N4: Q1.E, M1.pin_2
  N5: M1.pin_1, U3.+

custom parts:
  NodeMCU V3.0: ESP8266 based NodeMCU
  DHT11 Humitidy and Temperature Sensor: DHT11 Humidity and Temperature Sensor
